# Fritzing sketch sketch (saved by Fritzing 0.9.3b)
breadboards: 1

parts:
  Raspberry_Pi_1 = Raspberry Pi 3 [part_number=RPI-3-V1.2]
  R1 = Rotary Potentiometer (Small) [maximum_resistance=100kΩ package=THT]
  LCD1 = LCD screen

nets:
  GND: Raspberry_Pi_1.GND, R1.leg2, LCD1.VSS, LCD1.R/W, LCD1.LED-
  N1: Raspberry_Pi_1.GIPO19, LCD1.E
  N2: Raspberry_Pi_1.GIPO26, LCD1.RS
  N3: Raspberry_Pi_1.GIPO21, LCD1.DB4
  N4: Raspberry_Pi_1.GIPO20, LCD1.DB5
  N5: Raspberry_Pi_1.GIPO16, LCD1.DB6
  N6: Raspberry_Pi_1.GIPO12, LCD1.DB7
  5V: Raspberry_Pi_1.5V, R1.leg1, LCD1.VDD, LCD1.LED+
  N7: R1.wiper, LCD1.V0
